# Fritzing sketch devre_cizimi (saved by Fritzing 0.9.2b)

parts:
  Eleman1 = Arduino Nano (Rev3.0) (ICSP)
  GY-NEO6MV2 = SUP500F [package=sup500f]
  Part2 = Bluetooth HC-05 Macho

nets:
  N1: Eleman1.D1/TX, Part2.RXD
  N2: Eleman1.D0/RX, Part2.TXD
  N3: Eleman1.GND, GY-NEO6MV2.RX-I
  N4: Eleman1.D3, GY-NEO6MV2.GND
  N5: Eleman1.D4, GY-NEO6MV2.TX-O
  5V: Eleman1.5V, GY-NEO6MV2.VCC

notes:
  GND: Black
  VCC: Red
  RX: Yellow
  TX: Green
