# Fritzing sketch devre2 (saved by Fritzing 0.9.2b)
breadboards: 1

parts:
  S1 = Toggle Switch [package=THT]
  Arduino2 = Arduino Mini (Rev5)
  J1 = Infrared Proximity Sensor
  LED1 = LED - 3mm [color="Red (633nm)" package="3 mm [THT]"]
  R1 = Resistor [tolerance=±5% resistance=220 package="0603 [SMD]"]

nets:
  5V: S1.L1, Arduino2.5V, J1.Vcc
  N1: S1.L2, Arduino2.D7
  N2: Arduino2.D9_PWM, LED1.anode
  GND: Arduino2.GND, J1.GND, R1.Pin_1
  N3: LED1.cathode, R1.Pin_0
