# Fritzing sketch otg_motor_kontrol (saved by Fritzing 0.9.2b)

parts:
  Part1 = Arduino Uno (Rev3)
  920KV_Motor1 = DJI 920 KV Motor
  Power_plug2 = Power plug  # not connected
  M1 = ESC
  M2 = ESC
  920KV_Motor2 = DJI 920 KV Motor
  Power_plug3 = Power plug  # not connected

nets:
  GND: Part1.GND, M1.GND, M2.GND
  N1: Part1.D3_PWM, M1.DATA
  N2: Part1.D5_PWM, M2.DATA
  VIN: Part1.VIN, M1.5V
  N3: 920KV_Motor1.w, M1.W
  N4: 920KV_Motor1.v, M1.V
  N5: 920KV_Motor1.u, M1.U
  N6: M2.U, 920KV_Motor2.u
  N7: M2.V, 920KV_Motor2.v
  N8: M2.W, 920KV_Motor2.w

notes:
  MOTOR 1 BAĞLANTISI
  Bu kablolar rastgele bağlanır. Dönüş yönü ters ise her hangi iki kablonun yerini değiştirirsin.
  ESC
  Güç Kaynağı
  ADAPTER
  UNO
  MOTOR 2 BAĞLANTISI
  Bu kablolar rastgele bağlanır. Dönüş yönü ters ise her hangi iki kablonun yerini değiştirirsin.
  DİKKAT!!!
  Bu motorda ki kırmızı uç kesinlikle arduinoya gitmeyecek.

custom parts:
  DJI 920 KV Motor: DJI Brushless Outrunner 2212/920K Motor F330-550
