# Fritzing sketch RTC_bağlatı_şeması (saved by Fritzing 0.9.2b)

parts:
  Componente1 = Arduino Uno (Rev3)
  rtc = RTC_DS1302_module

nets:
  N1: Componente1.D10_PWM/SS, rtc.CLK
  N2: Componente1.D11_PWM/MOSI, rtc.DAT
  N3: Componente1.D12/MISO, rtc.RST

custom parts:
  RTC_DS1302_module: Arduino module DS1302 SPI Real Time Clock
