# Fritzing sketch keypad_buzzer_baglanti_semasi (saved by Fritzing 0.9.2b)

parts:
  Eleman1 = 4x4 Keypad [part_number=101207]
  Eleman2 = Arduino Uno (Rev3) - ICSP
  J1 = Piezo Speaker

nets:
  N1: Eleman1.1, Eleman2.D9_PWM
  N2: Eleman1.2, Eleman2.D8
  N3: Eleman1.3, Eleman2.D7
  N4: Eleman1.4, Eleman2.D6_PWM
  N5: Eleman1.5, Eleman2.D5_PWM
  N6: Eleman1.6, Eleman2.D4
  N7: Eleman1.7, Eleman2.D3_PWM
  N8: Eleman2.5V, J1.pin2
  N9: Eleman2.GND, J1.pin1

notes:
  Bu keypad 4X4 bu nedenle bir pinini boş bıraktım. Sen yine aynı sıra ile 7 pinini diziceksin.

custom parts:
  4x4 Keypad: Matrix membrane keypad 4x4
